// Logisim project bladeprod.circ as structural Verilog: 3 circuits, main circuit blademult
module blademult (
  input  [4:0] blade_2,
  input  [4:0] blade_1,
  input  [31:0] in_3,
  input  [31:0] in_4
);

  wire [31:0] n5_to_32_decoder_1_out_6;

  _5_to_32_Decoder u_5_to_32_decoder_1 (
    .s4(blade_2[4]), .s3(blade_2[3]), .s2(blade_2[2]), .s1(blade_2[1]), .s0(blade_2[0]),
    .out_6(n5_to_32_decoder_1_out_6));
  Multiplexer #(.select(5), .width(32), .enable("false")) multiplexer_1 (
    .in0({32{1'b1}}), .sel(blade_1));  // open: in1, in2, in3, in4, in5, in6, in7, in8, in9, in10, in11, in12, in13, in14, in15, in16, in17, in18, in19, in20, in21, in22, in23, in24, in25, in26, in27, in28, in29, in30, in31, out

  // Notes on the sheet:
  //   coefficient 1
  //   coefficient 2
endmodule

module _5_to_32_Decoder (
  input  s4,
  input  s3,
  input  s2,
  input  s1,
  input  s0,
  output [31:0] out_6
);

  wire not_1_out, not_2_out, not_3_out, not_4_out, not_5_out;

  not not_1 (not_1_out, s4);
  not not_2 (not_2_out, s2);
  not not_3 (not_3_out, s3);
  not not_4 (not_4_out, s1);
  not not_5 (not_5_out, s0);
  and _0 (out_6[0], not_5_out, not_4_out, not_2_out, not_3_out, not_1_out);
  and _1 (out_6[1], s0, not_4_out, not_2_out, not_3_out, not_1_out);
  and _2 (out_6[2], not_5_out, s1, not_2_out, not_3_out, not_1_out);
  and _3 (out_6[3], s0, s1, not_2_out, not_3_out, not_1_out);
  and _4 (out_6[4], not_5_out, not_4_out, s2, not_3_out, not_1_out);
  and _5 (out_6[5], s0, not_4_out, s2, not_3_out, not_1_out);
  and _6 (out_6[6], not_5_out, s1, s2, not_3_out, not_1_out);
  and _7 (out_6[7], s0, s1, s2, not_3_out, not_1_out);
  and _8 (out_6[8], not_5_out, not_4_out, not_2_out, s3, not_1_out);
  and _9 (out_6[9], s0, not_4_out, not_2_out, s3, not_1_out);
  and _10 (out_6[10], not_5_out, s1, not_2_out, s3, not_1_out);
  and _11 (out_6[11], s0, s1, not_2_out, s3, not_1_out);
  and _12 (out_6[12], not_5_out, not_4_out, s2, s3, not_1_out);
  and _13 (out_6[13], s0, not_4_out, s2, s3, not_1_out);
  and _14 (out_6[14], not_5_out, s1, s2, s3, not_1_out);
  and _15 (out_6[15], s0, s1, s2, s3, not_1_out);
  and _16 (out_6[16], not_5_out, not_4_out, not_2_out, not_3_out, s4);
  and _17 (out_6[17], s0, not_4_out, not_2_out, not_3_out, s4);
  and _18 (out_6[18], not_5_out, s1, not_2_out, not_3_out, s4);
  and _19 (out_6[19], s0, s1, not_2_out, not_3_out, s4);
  and _20 (out_6[20], not_5_out, not_4_out, s2, not_3_out, s4);
  and _21 (out_6[21], s0, not_4_out, s2, not_3_out, s4);
  and _22 (out_6[22], not_5_out, s1, s2, not_3_out, s4);
  and _23 (out_6[23], s0, s1, s2, not_3_out, s4);
  and _24 (out_6[24], not_5_out, not_4_out, not_2_out, s3, s4);
  and _25 (out_6[25], s0, not_4_out, not_2_out, s3, s4);
  and _26 (out_6[26], not_5_out, s1, not_2_out, s3, s4);
  and _27 (out_6[27], s0, s1, not_2_out, s3, s4);
  and _28 (out_6[28], not_5_out, not_4_out, s2, s3, s4);
  and _29 (out_6[29], s0, not_4_out, s2, s3, s4);
  and _30 (out_6[30], not_5_out, s1, s2, s3, s4);
  and _31 (out_6[31], s0, s1, s2, s3, s4);

  // Notes on the sheet:
  //   Least Significant Bit
  //   Output
endmodule

module conditionalIncrement (
  input  Enable,
  input  [31:0] in_2,
  output [31:0] out_3
);


  // Notes on the sheet:
  //   32 bit coefficient
endmodule
